// Digital circuit 16BitOR_gate.dig as structural Verilog
module _16BitOR_gate (
  input  [15:0] IN__16_Bits,
  input  [15:0] IN__16_Bits_2,
  output [15:0] OUT_16_Bits
);

  or or_1 (OUT_16_Bits[0], IN__16_Bits[0], IN__16_Bits_2[0]);
  or or_2 (OUT_16_Bits[1], IN__16_Bits[1], IN__16_Bits_2[1]);
  or or_3 (OUT_16_Bits[2], IN__16_Bits[2], IN__16_Bits_2[2]);
  or or_4 (OUT_16_Bits[3], IN__16_Bits[3], IN__16_Bits_2[3]);
  or or_5 (OUT_16_Bits[4], IN__16_Bits[4], IN__16_Bits_2[4]);
  or or_6 (OUT_16_Bits[5], IN__16_Bits[5], IN__16_Bits_2[5]);
  or or_7 (OUT_16_Bits[6], IN__16_Bits[6], IN__16_Bits_2[6]);
  or or_8 (OUT_16_Bits[7], IN__16_Bits[7], IN__16_Bits_2[7]);
  or or_9 (OUT_16_Bits[8], IN__16_Bits[8], IN__16_Bits_2[8]);
  or or_10 (OUT_16_Bits[9], IN__16_Bits[9], IN__16_Bits_2[9]);
  or or_11 (OUT_16_Bits[10], IN__16_Bits[10], IN__16_Bits_2[10]);
  or or_12 (OUT_16_Bits[11], IN__16_Bits[11], IN__16_Bits_2[11]);
  or or_13 (OUT_16_Bits[12], IN__16_Bits[12], IN__16_Bits_2[12]);
  or or_14 (OUT_16_Bits[13], IN__16_Bits[13], IN__16_Bits_2[13]);
  or or_15 (OUT_16_Bits[14], IN__16_Bits[14], IN__16_Bits_2[14]);
  or or_16 (OUT_16_Bits[15], IN__16_Bits[15], IN__16_Bits_2[15]);
endmodule
