// Digital circuit 16Bit_Adder.dig as structural Verilog
module _16Bit_Adder (
  input  [15:0] IN_A_16_BIT,
  input  [15:0] IN_B_16_BIT,
  output [15:0] OUT__16_BIT
);

  wire add_1_c_o, add_2_c_o, add_3_c_o, add_4_c_o, add_5_c_o, add_6_c_o, add_7_c_o, add_8_c_o, add_9_c_o,
       add_10_c_o, add_11_c_o, add_12_c_o, add_13_c_o, add_14_c_o, half_adder_1_carry;

  Half_Adder half_adder_1 (
    .IN_A(IN_A_16_BIT[0]), .IN_B(IN_B_16_BIT[0]), .SUM(OUT__16_BIT[0]), .CARRY(half_adder_1_carry));
  Add add_1 (.a(IN_A_16_BIT[1]), .b(IN_B_16_BIT[1]), .c_i(half_adder_1_carry), .s(OUT__16_BIT[1]), .c_o(add_1_c_o));
  Add add_2 (.a(IN_A_16_BIT[2]), .b(IN_B_16_BIT[2]), .c_i(add_1_c_o), .s(OUT__16_BIT[2]), .c_o(add_2_c_o));
  Add add_3 (.a(IN_A_16_BIT[3]), .b(IN_B_16_BIT[3]), .c_i(add_2_c_o), .s(OUT__16_BIT[3]), .c_o(add_3_c_o));
  Add add_4 (.a(IN_A_16_BIT[4]), .b(IN_B_16_BIT[4]), .c_i(add_3_c_o), .s(OUT__16_BIT[4]), .c_o(add_4_c_o));
  Add add_5 (.a(IN_A_16_BIT[5]), .b(IN_B_16_BIT[5]), .c_i(add_4_c_o), .s(OUT__16_BIT[5]), .c_o(add_5_c_o));
  Add add_6 (.a(IN_A_16_BIT[6]), .b(IN_B_16_BIT[6]), .c_i(add_5_c_o), .s(OUT__16_BIT[6]), .c_o(add_6_c_o));
  Add add_7 (.a(IN_A_16_BIT[7]), .b(IN_B_16_BIT[7]), .c_i(add_6_c_o), .s(OUT__16_BIT[7]), .c_o(add_7_c_o));
  Add add_8 (.a(IN_A_16_BIT[8]), .b(IN_B_16_BIT[8]), .c_i(add_7_c_o), .s(OUT__16_BIT[8]), .c_o(add_8_c_o));
  Add add_9 (.a(IN_A_16_BIT[9]), .b(IN_B_16_BIT[9]), .c_i(add_8_c_o), .s(OUT__16_BIT[9]), .c_o(add_9_c_o));
  Add add_10 (.a(IN_A_16_BIT[10]), .b(IN_B_16_BIT[10]), .c_i(add_9_c_o), .s(OUT__16_BIT[10]), .c_o(add_10_c_o));
  Add add_11 (.a(IN_A_16_BIT[11]), .b(IN_B_16_BIT[11]), .c_i(add_10_c_o), .s(OUT__16_BIT[11]), .c_o(add_11_c_o));
  Add add_12 (.a(IN_A_16_BIT[12]), .b(IN_B_16_BIT[12]), .c_i(add_11_c_o), .s(OUT__16_BIT[12]), .c_o(add_12_c_o));
  Add add_13 (.a(IN_A_16_BIT[13]), .b(IN_B_16_BIT[13]), .c_i(add_12_c_o), .s(OUT__16_BIT[13]), .c_o(add_13_c_o));
  Add add_14 (.a(IN_A_16_BIT[14]), .b(IN_B_16_BIT[14]), .c_i(add_13_c_o), .s(OUT__16_BIT[14]), .c_o(add_14_c_o));
  Add add_15 (.a(IN_A_16_BIT[15]), .b(IN_B_16_BIT[15]), .c_i(add_14_c_o), .s(OUT__16_BIT[15]));  // open: c_o
endmodule
