// Digital circuit 16bitMUX_gate.dig as structural Verilog
module _16bitMUX_gate (
  input  [15:0] IN_A_16_BIT,
  input  [15:0] IN_B_16_BIT,
  input  SEL,
  output [15:0] OUT_16_BIT
);

  Multiplexer multiplexer_1 (.sel(SEL), .in_0(IN_A_16_BIT[0]), .in_1(IN_B_16_BIT[0]), .out(OUT_16_BIT[0]));
  Multiplexer multiplexer_2 (.sel(SEL), .in_0(IN_A_16_BIT[1]), .in_1(IN_B_16_BIT[1]), .out(OUT_16_BIT[1]));
  Multiplexer multiplexer_3 (.sel(SEL), .in_0(IN_A_16_BIT[2]), .in_1(IN_B_16_BIT[2]), .out(OUT_16_BIT[2]));
  Multiplexer multiplexer_4 (.sel(SEL), .in_0(IN_A_16_BIT[3]), .in_1(IN_B_16_BIT[3]), .out(OUT_16_BIT[3]));
  Multiplexer multiplexer_5 (.sel(SEL), .in_0(IN_A_16_BIT[4]), .in_1(IN_B_16_BIT[4]), .out(OUT_16_BIT[4]));
  Multiplexer multiplexer_6 (.sel(SEL), .in_0(IN_A_16_BIT[5]), .in_1(IN_B_16_BIT[5]), .out(OUT_16_BIT[5]));
  Multiplexer multiplexer_7 (.sel(SEL), .in_0(IN_A_16_BIT[6]), .in_1(IN_B_16_BIT[6]), .out(OUT_16_BIT[6]));
  Multiplexer multiplexer_8 (.sel(SEL), .in_0(IN_A_16_BIT[7]), .in_1(IN_B_16_BIT[7]), .out(OUT_16_BIT[7]));
  Multiplexer multiplexer_9 (.sel(SEL), .in_0(IN_A_16_BIT[8]), .in_1(IN_B_16_BIT[8]), .out(OUT_16_BIT[8]));
  Multiplexer multiplexer_10 (.sel(SEL), .in_0(IN_A_16_BIT[9]), .in_1(IN_B_16_BIT[9]), .out(OUT_16_BIT[9]));
  Multiplexer multiplexer_11 (.sel(SEL), .in_0(IN_A_16_BIT[10]), .in_1(IN_B_16_BIT[10]), .out(OUT_16_BIT[10]));
  Multiplexer multiplexer_12 (.sel(SEL), .in_0(IN_A_16_BIT[11]), .in_1(IN_B_16_BIT[11]), .out(OUT_16_BIT[11]));
  Multiplexer multiplexer_13 (.sel(SEL), .in_0(IN_A_16_BIT[12]), .in_1(IN_B_16_BIT[12]), .out(OUT_16_BIT[12]));
  Multiplexer multiplexer_14 (.sel(SEL), .in_0(IN_A_16_BIT[13]), .in_1(IN_B_16_BIT[13]), .out(OUT_16_BIT[13]));
  Multiplexer multiplexer_15 (.sel(SEL), .in_0(IN_A_16_BIT[14]), .in_1(IN_B_16_BIT[14]), .out(OUT_16_BIT[14]));
  Multiplexer multiplexer_16 (.sel(SEL), .in_0(IN_A_16_BIT[15]), .in_1(IN_B_16_BIT[15]), .out(OUT_16_BIT[15]));
endmodule
