// Digital circuit 16bitNOT_gate.dig as structural Verilog
module _16bitNOT_gate (
  input  [15:0] IN,
  output [15:0] OUT
);

  nand nand_1 (OUT[0], IN[0], IN[0]);
  nand nand_2 (OUT[1], IN[1], IN[1]);
  nand nand_3 (OUT[2], IN[2], IN[2]);
  nand nand_4 (OUT[3], IN[3], IN[3]);
  nand nand_5 (OUT[4], IN[4], IN[4]);
  nand nand_6 (OUT[5], IN[5], IN[5]);
  nand nand_7 (OUT[6], IN[6], IN[6]);
  nand nand_8 (OUT[7], IN[7], IN[7]);
  nand nand_9 (OUT[8], IN[8], IN[8]);
  nand nand_10 (OUT[9], IN[9], IN[9]);
  nand nand_11 (OUT[10], IN[10], IN[10]);
  nand nand_12 (OUT[11], IN[11], IN[11]);
  nand nand_13 (OUT[12], IN[12], IN[12]);
  nand nand_14 (OUT[13], IN[13], IN[13]);
  nand nand_15 (OUT[14], IN[14], IN[14]);
  nand nand_16 (OUT[15], IN[15], IN[15]);
endmodule
