// Digital circuit 1Bit_Register.dig as structural Verilog
module _1Bit_Register (
  input  Clock,
  input  LOAD,
  input  IN,
  output OUT
);

  wire multiplexer_1_out;

  Multiplexer multiplexer_1 (.sel(LOAD), .in_0(OUT), .in_1(IN), .out(multiplexer_1_out));
  D_FF d_ff_1 (.D(multiplexer_1_out), .C(Clock), .Q(OUT));  // open: nQ
endmodule
