// Digital circuit 2x1MUX_gate.dig as structural Verilog
module _2x1MUX_gate (
  input  IN_A,
  input  IN_B,
  input  SEL,
  output OUT
);

  wire nand_1_out, nand_2_out, nand_3_out;

  nand nand_1 (nand_1_out, SEL, SEL);
  nand nand_2 (nand_2_out, nand_1_out, IN_A);
  nand nand_3 (nand_3_out, SEL, IN_B);
  nand nand_4 (OUT, nand_2_out, nand_3_out);
endmodule
