// Digital circuit 4WayDEMUX.dig as structural Verilog
module _4WayDEMUX (
  input  IN,
  input  [1:0] SEL,
  output OUT_B,
  output OUT_A,
  output OUT_C,
  output OUT_D
);

  wire demultiplexer_1_out_0, demultiplexer_1_out_1;

  Demultiplexer demultiplexer_1 (.sel(SEL[1]), .in(IN), .out_0(demultiplexer_1_out_0), .out_1(demultiplexer_1_out_1));
  Demultiplexer demultiplexer_2 (.sel(SEL[0]), .in(demultiplexer_1_out_0), .out_0(OUT_A), .out_1(OUT_B));
  Demultiplexer demultiplexer_3 (.sel(SEL[0]), .in(demultiplexer_1_out_1), .out_0(OUT_C), .out_1(OUT_D));
endmodule
