// Digital circuit 8WayOR_gate.dig as structural Verilog
module _8WayOR_gate (
  input  [7:0] IN_8_BIT,
  output OUT_1_BIT
);

  wire or_1_out, or_2_out, or_3_out, or_4_out, or_5_out, or_6_out;

  or or_1 (or_1_out, IN_8_BIT[0], IN_8_BIT[1]);
  or or_2 (or_2_out, IN_8_BIT[2], IN_8_BIT[3]);
  or or_3 (or_3_out, IN_8_BIT[4], IN_8_BIT[5]);
  or or_4 (or_4_out, IN_8_BIT[6], IN_8_BIT[7]);
  or or_5 (or_5_out, or_1_out, or_2_out);
  or or_6 (or_6_out, or_3_out, or_4_out);
  or or_7 (OUT_1_BIT, or_5_out, or_6_out);
endmodule
