// Digital circuit 8wayDMUX.dig as structural Verilog
module _8wayDMUX (
  input  IN,
  input  [2:0] SEL,
  output OUT_A,
  output OUT_B,
  output OUT_C,
  output OUT_D,
  output OUT_E,
  output OUT_F,
  output OUT_G,
  output OUT_H
);

  wire demultiplexer_1_out_0, demultiplexer_1_out_1, demultiplexer_2_out_0, demultiplexer_2_out_1,
       demultiplexer_3_out_0, demultiplexer_3_out_1;

  Demultiplexer demultiplexer_1 (.sel(SEL[2]), .in(IN), .out_0(demultiplexer_1_out_0), .out_1(demultiplexer_1_out_1));
  Demultiplexer demultiplexer_2 (
    .sel(SEL[1]), .in(demultiplexer_1_out_0), .out_0(demultiplexer_2_out_0), .out_1(demultiplexer_2_out_1));
  Demultiplexer demultiplexer_3 (
    .sel(SEL[1]), .in(demultiplexer_1_out_1), .out_0(demultiplexer_3_out_0), .out_1(demultiplexer_3_out_1));
  Demultiplexer demultiplexer_4 (.sel(SEL[0]), .in(demultiplexer_2_out_0), .out_0(OUT_A), .out_1(OUT_B));
  Demultiplexer demultiplexer_5 (.sel(SEL[0]), .in(demultiplexer_2_out_1), .out_0(OUT_C), .out_1(OUT_D));
  Demultiplexer demultiplexer_6 (.sel(SEL[0]), .in(demultiplexer_3_out_0), .out_0(OUT_E), .out_1(OUT_F));
  Demultiplexer demultiplexer_7 (.sel(SEL[0]), .in(demultiplexer_3_out_1), .out_0(OUT_G), .out_1(OUT_H));
endmodule
