// Digital circuit ALU.dig as structural Verilog
module ALU (
  input  [15:0] x__16_Bit,
  input  [15:0] y__16_bit,
  input  zx,
  input  nx,
  input  zy,
  input  ny,
  input  f,
  input  no,
  output [15:0] OUT__16_bit,
  output zr,
  output ng
);

  wire or_1_out, or_2_out, or_3_out;
  wire [15:0] add_1_s, and_1_out, multiplexer_1_out, multiplexer_2_out, multiplexer_3_out, multiplexer_4_out,
       multiplexer_5_out, not_1_out, not_2_out, not_4_out;

  Multiplexer #(.Bits(16)) multiplexer_1 (.sel(zx), .in_0(x__16_Bit), .in_1({16{1'b0}}), .out(multiplexer_1_out));
  Multiplexer #(.Bits(16)) multiplexer_2 (.sel(zy), .in_0(y__16_bit), .in_1({16{1'b0}}), .out(multiplexer_2_out));
  assign not_1_out = ~multiplexer_1_out;  // Not not_1, 16 bits wide
  assign not_2_out = ~multiplexer_2_out;  // Not not_2, 16 bits wide
  or or_1 (or_1_out, OUT__16_bit[0], OUT__16_bit[4]);
  or or_2 (or_2_out, OUT__16_bit[8], OUT__16_bit[12]);
  Multiplexer #(.Bits(16)) multiplexer_3 (
    .sel(nx), .in_0(multiplexer_1_out), .in_1(not_1_out), .out(multiplexer_3_out));
  Multiplexer #(.Bits(16)) multiplexer_4 (
    .sel(ny), .in_0(multiplexer_2_out), .in_1(not_2_out), .out(multiplexer_4_out));
  assign and_1_out = multiplexer_3_out & multiplexer_4_out;  // And and_1, 16 bits wide
  Add #(.Bits(16)) add_1 (.a(multiplexer_3_out), .b(multiplexer_4_out), .c_i(1'b0), .s(add_1_s));  // open: c_o
  or or_3 (or_3_out, or_1_out, or_2_out);
  Multiplexer #(.Bits(16)) multiplexer_5 (.sel(f), .in_0(and_1_out), .in_1(add_1_s), .out(multiplexer_5_out));
  not not_3 (zr, or_3_out);
  assign not_4_out = ~multiplexer_5_out;  // Not not_4, 16 bits wide
  Multiplexer #(.Bits(16)) multiplexer_6 (
    .sel(no), .in_0(multiplexer_5_out), .in_1(not_4_out), .out({ng, OUT__16_bit[14:0]}));

  assign OUT__16_bit[15] = ng;
endmodule
