// Digital circuit Full_Adder.dig as structural Verilog
module Full_Adder (
  input  IN_A,
  input  IN_B,
  input  IN_C,
  output SUM,
  output CARRY
);

  wire and_1_out, and_2_out, xor_1_out;

  xor xor_1 (xor_1_out, IN_A, IN_B);
  and and_1 (and_1_out, IN_A, IN_B);
  and and_2 (and_2_out, IN_C, xor_1_out);
  xor xor_2 (SUM, xor_1_out, IN_C);
  or or_1 (CARRY, and_1_out, and_2_out);
endmodule
