// Digital circuit Half_Adder.dig as structural Verilog
module Half_Adder (
  input  IN_A,
  input  IN_B,
  output SUM,
  output CARRY
);

  xor xor_1 (SUM, IN_A, IN_B);
  and and_1 (CARRY, IN_A, IN_B);
endmodule
