// Digital circuit xor_gate.dig as structural Verilog
module xor_gate (
  input  IN_A,
  input  IN_B,
  output OUT
);

  wire nand_1_out, nand_2_out, nand_3_out;

  nand nand_1 (nand_1_out, IN_A, IN_B);
  nand nand_2 (nand_2_out, IN_A, nand_1_out);
  nand nand_3 (nand_3_out, nand_1_out, IN_B);
  nand nand_4 (OUT, nand_2_out, nand_3_out);
endmodule
