// Digital circuit and_gate.dig as structural Verilog
module and_gate (
  input  IN_A,
  input  IN_B,
  output OUT
);

  wire nand_1_out;

  nand nand_1 (nand_1_out, IN_A, IN_B);
  nand nand_2 (OUT, nand_1_out, nand_1_out);
endmodule
