// Digital circuit demux_gate.dig as structural Verilog
module demux_gate (
  input  IN,
  input  SEL,
  output OUT_A,
  output OUT_B
);

  wire nand_1_out, nand_2_out, nand_3_out;

  nand nand_1 (nand_1_out, SEL, SEL);
  nand nand_2 (nand_2_out, IN, nand_1_out);
  nand nand_3 (nand_3_out, SEL, IN);
  nand nand_4 (OUT_A, nand_2_out, nand_2_out);
  nand nand_5 (OUT_B, nand_3_out, nand_3_out);
endmodule
