// Digital circuit or_gate.dig as structural Verilog
module or_gate (
  input  IN_A,
  input  IN_B,
  output OUT
);

  wire nand_1_out, nand_2_out;

  nand nand_1 (nand_1_out, IN_A, IN_A);
  nand nand_2 (nand_2_out, IN_B, IN_B);
  nand nand_3 (OUT, nand_1_out, nand_2_out);
endmodule
